# Fritzing sketch sensor_connection_diagram (saved by Fritzing 0.9.3b)

parts:
  Raspberry_Pi_1 = Raspberry Pi 3 [part_number=RPI-3-V1.2]
  Part1 = NeoPixel Stick [part_number=1426]
  U1 = SUP500F [package=sup500f]
  VCC1 = Battery block 9V
  U2 = Mini-360 DC-DC Buck converter [package=THT]
  X1 = USB Connectors [package=usb-microb]
  U3 = NodeMCU V3.0  # not connected

nets:
  3V3: Raspberry_Pi_1.3v3, Part1.+5V
  GND: Raspberry_Pi_1.GND, Part1.GND, U1.GND
  N1: Raspberry_Pi_1.GIPO20, U1.TX-O
  N2: Raspberry_Pi_1.GIPO12, Part1.DATAIN
  5V: Raspberry_Pi_1.5V, U1.VCC
  N3: VCC1.-, U2.IN-
  N4: VCC1.+, U2.IN+
  N5: U2.OUT+, X1.VBUS
  N6: U2.OUT-, X1.GND

notes:
  Pi Camera is Directly Connected to Camera Slot.
  Panasonic 26 V Battery
  Generic Voltage Regulator StepDown 26 V -> 5V
  Gives Power Direclty to Micro USB connection on RBP
  Addressable RGB LED Strip. Used as Indicartor for User and Debugging
  GPS Unit Connects through Softaware TX-RX
  ESP Based terMITe Sensor (MIT). Connects dircelty to USB port on Raspberry Pi.
  Motor Unit Is connected with Raspberry PI using Hardware RX and TX pins.

custom parts:
  NeoPixel Stick: Make your own little LED strip arrangement with this stick of NeoPixel LEDs. We crammed 8 of the tiny 5050 (5mm x 5mm) smart RGB LEDs onto a PCB with mounting holes and a chainable design. Use only one microcontroller pin to control as many as you can chain together! Each LED is addressable as the driver chip is inside the LED. Each one has ~18mA constant current drive so the color will be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
  Mini-360 DC-DC Buck converter: Mini-360 DC-DC Buck converter. Tiny buck step down voltage converter, input voltage 4.75 to 23V output 1 to 17V adjustable. Available from ebay and the like.
  NodeMCU V3.0: ESP8266 based NodeMCU
